// Logisim project FBUCPU.circ as structural Verilog: 1 circuit, main circuit main
module main (
);

  wire ADD2, Clk, comparator_1_eq, DIV5, DR7, DR8, DR9, DRE, DRK, LOD0, MUL4, multiplexer_6_out, RAMWrNext3,
       Rst, STO1, SUB3;
  wire [2:0] durum, durumNext0, durumNext1, durumNext2, multiplexer_1_out, multiplexer_21_out,
       multiplexer_22_out, multiplexer_23_out, multiplexer_24_out;
  wire [5:0] MAR, MARNext0, MARNext1, MARNext2, MARNext3, multiplexer_2_out, multiplexer_5_out,
       multiplexer_9_out, multiplexer_12_out, pcNext1, pcNext2;
  wire [9:0] ACC, ACCNext3, IR, IRNext1, MDRIn, MDRInNext3, multiplexer_3_out, multiplexer_4_out,
       multiplexer_8_out, multiplexer_10_out, multiplexer_13_out, multiplexer_15_out, multiplexer_16_out,
       Sonuc2, Sonuc3, Sonuc4, Sonuc5;

  Button Reset (.out(Rst));
  Clock SaatClk (.out(Clk));
  Multiplexer #(.select(3), .width(3), .enable("false")) multiplexer_1 (
    .in0(durumNext0), .in1(durumNext1), .in2(durumNext2), .in3(3'b000), .in4(durum), .in5(3'b000),
    .in6(3'b000), .in7(3'b000), .out(multiplexer_1_out), .sel(durum));
  Multiplexer #(.select(3), .width(6), .enable("false")) multiplexer_2 (
    .in0(MARNext0), .in1(pcNext1), .in2(pcNext2), .in3(MARNext0), .in4(MARNext0), .in5({6{1'b0}}),
    .in6({6{1'b0}}), .in7({6{1'b0}}), .out(multiplexer_2_out), .sel(durum));
  Multiplexer #(.select(3), .width(10), .enable("false")) multiplexer_3 (
    .in0(IR), .in1(IRNext1), .in2(IR), .in3(IR), .in4(IR), .in5({10{1'b0}}), .in6({10{1'b0}}),
    .in7({10{1'b0}}), .out(multiplexer_3_out), .sel(durum));
  Multiplexer #(.select(3), .width(10), .enable("false")) multiplexer_4 (
    .in0(ACC), .in1(ACC), .in2(ACC), .in3(ACCNext3), .in4(ACC), .in5({10{1'b0}}), .in6({10{1'b0}}),
    .in7({10{1'b0}}), .out(multiplexer_4_out), .sel(durum));
  Register #(.width(3)) register_1 (.D(multiplexer_1_out), .en(1'b1), .clk(Clk), .Q(durum), .clr(Rst));
  Register #(.width(6)) register_2 (.D(multiplexer_2_out), .en(1'b1), .clk(Clk), .Q(MARNext0), .clr(Rst));
  Register #(.width(10)) register_3 (.D(multiplexer_3_out), .en(1'b1), .clk(Clk), .Q(IR), .clr(Rst));
  Register #(.width(10)) register_4 (.D(multiplexer_4_out), .en(1'b1), .clk(Clk), .Q(ACC), .clr(Rst));
  Multiplexer #(.select(3), .width(6), .enable("false")) multiplexer_5 (
    .in0(MARNext0), .in1(MARNext1), .in2(MARNext2), .in3(MARNext3), .in4({6{1'b0}}), .in5({6{1'b0}}),
    .in6({6{1'b0}}), .in7({6{1'b0}}), .out(multiplexer_5_out), .sel(durum));
  Multiplexer #(.select(3), .enable("false")) multiplexer_6 (
    .in0(1'b0), .in1(1'b0), .in2(1'b0), .in3(RAMWrNext3), .in4(1'b0), .in5(1'b0), .in6(1'b0), .in7(1'b0),
    .out(multiplexer_6_out), .sel(durum));
  Multiplexer #(.select(3), .width(10), .enable("false")) multiplexer_7 (
    .in0({10{1'b0}}), .in1({10{1'b0}}), .in2({10{1'b0}}), .in3(MDRInNext3), .in4({10{1'b0}}),
    .in5({10{1'b0}}), .in6({10{1'b0}}), .in7({10{1'b0}}), .out(MDRIn), .sel(durum));
  RAM #(.addrWidth(6), .dataWidth(10), .databus("bibus")) RAM10Bit (
    .addr(multiplexer_5_out), .we(multiplexer_6_out), .oe(1'b1), .clk(Clk), .din(MDRIn), .dout(IRNext1));
  Multiplexer #(.width(10), .enable("false")) multiplexer_8 (
    .in0(ACC), .in1(IRNext1), .out(multiplexer_8_out), .sel(LOD0));
  Multiplexer #(.width(6), .enable("false")) multiplexer_9 (
    .in0(MARNext0), .in1(IR[5:0]), .out(multiplexer_9_out), .sel(comparator_1_eq));
  Comparator #(.width(10)) comparator_1 (.a(ACC), .b({10{1'b0}}), .eq(comparator_1_eq));  // open: gt, lt
  Adder #(.width(3)) adder_1 (.a(durum), .b(3'b001), .out(durumNext0));  // open: cin, cout
  Adder #(.width(3)) adder_2 (.a(durum), .b(3'b001), .out(durumNext1));  // open: cin, cout
  Adder #(.width(6)) adder_3 (.a(MARNext0), .b(6'b000001), .out(pcNext1));  // open: cin, cout
  Multiplexer #(.width(10), .enable("false")) multiplexer_10 (
    .in0(multiplexer_8_out), .in1(ACC), .out(multiplexer_10_out), .sel(STO1));
  Multiplexer #(.enable("false")) multiplexer_11 (.in0(1'b0), .in1(1'b1), .out(RAMWrNext3), .sel(STO1));
  Multiplexer #(.width(6), .enable("false")) multiplexer_12 (
    .in0(MARNext0), .in1(multiplexer_9_out), .out(multiplexer_12_out), .sel(DR7));
  Multiplexer #(.width(10), .enable("false")) multiplexer_13 (
    .in0(multiplexer_10_out), .in1(Sonuc2), .out(multiplexer_13_out), .sel(ADD2));
  Multiplexer #(.width(6), .enable("false")) multiplexer_14 (
    .in0(multiplexer_12_out), .in1(IR[5:0]), .out(pcNext2), .sel(DRE));
  Multiplexer #(.width(10), .enable("false")) multiplexer_15 (
    .in0(multiplexer_13_out), .in1(Sonuc3), .out(multiplexer_15_out), .sel(SUB3));
  Multiplexer #(.width(10), .enable("false")) multiplexer_16 (
    .in0(multiplexer_15_out), .in1(Sonuc4), .out(multiplexer_16_out), .sel(MUL4));
  Multiplexer #(.width(10), .enable("false")) multiplexer_17 (.in0(ACC), .in1(ACCNext3), .out(MDRInNext3), .sel(STO1));
  Comparator #(.width(4), .mode("unsigned")) comparator_2 (.a(IR[9:6]), .b(4'b0110), .eq(DRE), .lt(DRK));  // open: gt
  Comparator #(.width(4), .mode("unsigned")) comparator_3 (.a(IR[9:6]), .b(4'b1001), .eq(DR9));  // open: gt, lt
  Multiplexer #(.width(10), .enable("false")) multiplexer_18 (
    .in0(multiplexer_16_out), .in1(Sonuc5), .out(ACCNext3), .sel(DIV5));
  Comparator #(.width(4), .mode("unsigned")) comparator_4 (.a(IR[9:6]), .b(4'b1000), .eq(DR8));  // open: gt, lt
  Comparator #(.width(4), .mode("unsigned")) comparator_5 (.a(IR[9:6]), .b(4'b0111), .eq(DR7));  // open: gt, lt
  Comparator #(.width(4)) comparator_6 (.a(IR[9:6]), .b(4'b0000), .eq(LOD0));  // open: gt, lt
  Comparator #(.width(4)) comparator_7 (.a(IR[9:6]), .b(4'b0011), .eq(SUB3));  // open: gt, lt
  Multiplexer #(.width(6), .enable("false")) multiplexer_19 (.in0(MAR), .in1(IR[5:0]), .out(MARNext3), .sel(STO1));
  Comparator #(.width(4)) comparator_8 (.a(IR[9:6]), .b(4'b0001), .eq(STO1));  // open: gt, lt
  Comparator #(.width(4)) comparator_9 (.a(IR[9:6]), .b(4'b0100), .eq(MUL4));  // open: gt, lt
  Multiplexer #(.width(6), .enable("false")) multiplexer_20 (.in0(MAR), .in1(IR[5:0]), .out(MARNext2), .sel(DRK));
  Comparator #(.width(4)) comparator_10 (.a(IR[9:6]), .b(4'b0010), .eq(ADD2));  // open: gt, lt
  Comparator #(.width(4)) comparator_11 (.a(IR[9:6]), .b(4'b0101), .eq(DIV5));  // open: gt, lt
  Divider #(.width(10)) divider_1 (.a(ACC), .b(IRNext1), .out(Sonuc5));  // open: upper, rem
  Multiplexer #(.width(3), .enable("false")) multiplexer_21 (
    .in0(durum), .in1(3'b011), .out(multiplexer_21_out), .sel(DRK));
  Subtractor #(.width(10)) subtractor_1 (.a(ACC), .b(IRNext1), .out(Sonuc3));  // open: bin, bout
  Multiplexer #(.width(3), .enable("false")) multiplexer_22 (
    .in0(multiplexer_21_out), .in1(3'b000), .out(multiplexer_22_out), .sel(DRE));
  Multiplexer #(.width(3), .enable("false")) multiplexer_23 (
    .in0(multiplexer_22_out), .in1(3'b000), .out(multiplexer_23_out), .sel(DR7));
  Multiplexer #(.width(3), .enable("false")) multiplexer_24 (
    .in0(multiplexer_23_out), .in1(3'b000), .out(multiplexer_24_out), .sel(DR8));
  Multiplier #(.width(10)) multiplier_1 (.a(IRNext1), .b(ACC), .out(Sonuc4));  // open: cin, cout
  Adder #(.width(10)) adder_4 (.a(ACC), .b(IRNext1), .out(Sonuc2));  // open: cin, cout
  Multiplexer #(.width(3), .enable("false")) multiplexer_25 (
    .in0(multiplexer_24_out), .in1(3'b100), .out(durumNext2), .sel(DR9));

  // Other names for the same wires on the sheet: ACCNext0[9:0] = ACC; ACCNext1[9:0] = ACC; ACCNext2[9:0] = ACC;
  //   ACCNext4[9:0] = ACC; durumNext4[2:0] = durum; IRNext0[9:0] = IR; IRNext2[9:0] = IR; IRNext3[9:0] = IR;
  //   IRNext4[9:0] = IR; MDROut[9:0] = IRNext1; PC[5:0] = MARNext0; pcNext0[5:0] = MARNext0; pcNext3[5:0] = MARNext0;
  //   pcNext4[5:0] = MARNext0

  // Notes on the sheet:
  //   durum
  //   PC
  //   IR
  //   ACC
  //   durumNext
  //   PCNext
  //   IRNext
  //   ACCNext
  //   RAMWr
  //   MDRIn
  //   durum2
  //   durum0
  //   durum1
  //   durum3
  //   durum4
  //   -----------------------------------------------------------------
  //   -----------------------------------------------------------------
  //   -----------------------------------------------------------------
  //   -----------------------------------------------------------------
  //   -----------------------------------------------------------------
  //   -----------------------------------------------------------------
  //   -----------------------------------------------------------------
  //   -----------------------------------------------------------------
  //   -----------------------------------------------------------------
  //   -----------------------------------------------------------------
  //   -----------------------------------------------------------------
  //   -----------------------------------------------------------------
endmodule
