// Logisim project proje.circ as structural Verilog: 1 circuit, main circuit main
module main (
);

  wire Clk, multiplexer_6_out, Rst;
  wire [2:0] durum, durumNext0, durumNext1, multiplexer_1_out;
  wire [5:0] MARNext0, MARNext1, multiplexer_2_out, multiplexer_5_out, pcNext1;
  wire [9:0] ACC, IR, IRNext1, MDRIn, multiplexer_3_out, multiplexer_4_out;

  Button Reset (.out(Rst));
  Clock SaatClk (.out(Clk));
  Multiplexer #(.select(3), .width(3), .enable("false")) multiplexer_1 (
    .in0(durumNext0), .in1(durumNext1), .in2(3'b000), .in3(3'b000), .in4(durum), .in5(3'b000), .in6(3'b000),
    .in7(3'b000), .out(multiplexer_1_out), .sel(durum));
  Multiplexer #(.select(3), .width(6), .enable("false")) multiplexer_2 (
    .in0(MARNext0), .in1(pcNext1), .in2(MARNext0), .in3(MARNext0), .in4(MARNext0), .in5({6{1'b0}}),
    .in6({6{1'b0}}), .in7({6{1'b0}}), .out(multiplexer_2_out), .sel(durum));
  Multiplexer #(.select(3), .width(10), .enable("false")) multiplexer_3 (
    .in0(IR), .in1(IRNext1), .in2(IR), .in3(IR), .in4(IR), .in5({10{1'b0}}), .in6({10{1'b0}}),
    .in7({10{1'b0}}), .out(multiplexer_3_out), .sel(durum));
  Multiplexer #(.select(3), .width(10), .enable("false")) multiplexer_4 (
    .in0(ACC), .in1(ACC), .in2(ACC), .in3(ACC), .in4(ACC), .in5({10{1'b0}}), .in6({10{1'b0}}),
    .in7({10{1'b0}}), .out(multiplexer_4_out), .sel(durum));
  Register #(.width(3)) register_1 (.D(multiplexer_1_out), .en(1'b1), .clk(Clk), .Q(durum), .clr(Rst));
  Register #(.width(6)) register_2 (.D(multiplexer_2_out), .en(1'b1), .clk(Clk), .Q(MARNext0), .clr(Rst));
  Register #(.width(10)) register_3 (.D(multiplexer_3_out), .en(1'b1), .clk(Clk), .Q(IR), .clr(Rst));
  Register #(.width(10)) register_4 (.D(multiplexer_4_out), .en(1'b1), .clk(Clk), .Q(ACC), .clr(Rst));
  Multiplexer #(.select(3), .width(6), .enable("false")) multiplexer_5 (
    .in0(MARNext0), .in1(MARNext1), .in2({6{1'b0}}), .in3({6{1'b0}}), .in4({6{1'b0}}), .in5({6{1'b0}}),
    .in6({6{1'b0}}), .in7({6{1'b0}}), .out(multiplexer_5_out), .sel(durum));
  Multiplexer #(.select(3), .enable("false")) multiplexer_6 (
    .in0(1'b0), .in1(1'b0), .in2(1'b0), .in3(1'b0), .in4(1'b0), .in5(1'b0), .in6(1'b0), .in7(1'b0),
    .out(multiplexer_6_out), .sel(durum));
  Multiplexer #(.select(3), .width(10), .enable("false")) multiplexer_7 (
    .in0({10{1'b0}}), .in1({10{1'b0}}), .in2({10{1'b0}}), .in3(MDRIn), .in4({10{1'b0}}), .in5({10{1'b0}}),
    .in6({10{1'b0}}), .in7({10{1'b0}}), .out(MDRIn), .sel(durum));
  RAM #(.addrWidth(6), .dataWidth(10), .databus("bibus")) RAM10Bit (
    .addr(multiplexer_5_out), .we(multiplexer_6_out), .oe(1'b1), .clk(Clk), .din(MDRIn), .dout(IRNext1));
  Adder #(.width(3)) adder_1 (.a(durum), .b(3'b001), .out(durumNext0));  // open: cin, cout
  Adder #(.width(3)) adder_2 (.a(durum), .b(3'b001), .out(durumNext1));  // open: cin, cout
  Adder #(.width(6)) adder_3 (.a(MARNext0), .b(6'b000001), .out(pcNext1));  // open: cin, cout

  // Other names for the same wires on the sheet: ACCNext0[9:0] = ACC; ACCNext1[9:0] = ACC; ACCNext2[9:0] = ACC;
  //   ACCNext3[9:0] = ACC; ACCNext4[9:0] = ACC; durumNext4[2:0] = durum; IRNext0[9:0] = IR; IRNext2[9:0] = IR;
  //   IRNext3[9:0] = IR; IRNext4[9:0] = IR; MDRInNext3[9:0] = MDRIn; MDROut[9:0] = IRNext1; PC[5:0] = MARNext0;
  //   pcNext0[5:0] = MARNext0; pcNext2[5:0] = MARNext0; pcNext3[5:0] = MARNext0; pcNext4[5:0] = MARNext0

  // Notes on the sheet:
  //   durum
  //   PC
  //   IR
  //   ACC
  //   durumNext
  //   PCNext
  //   IRNext
  //   ACCNext
  //   MAR
  //   RAMWr
  //   MDRIn
  //   durum0
  //   durum1
  //   durum2
  //   durum3
  //   durum4
  //   -----------------------------------------------------------------
  //   -----------------------------------------------------------------
  //   -----------------------------------------------------------------
  //   -----------------------------------------------------------------
  //   -----------------------------------------------------------------
  //   -----------------------------------------------------------------
  //   -----------------------------------------------------------------
  //   -----------------------------------------------------------------
  //   -----------------------------------------------------------------
  //   -----------------------------------------------------------------
  //   -----------------------------------------------------------------
  //   -----------------------------------------------------------------
endmodule
